# Fritzing sketch schema (saved by Fritzing 0.8.5b)
breadboards: 1

parts:
  Spannungsregler = 4 x AAA Battery Mount
  Raspberry/Galileo_Board = Mystery Part - 2 pins [chip_label="SoC Board" package=THT]
  Amperemeter = Amperemeter

nets:
  N1: Spannungsregler.-, Raspberry/Galileo_Board.GND
  N2: Spannungsregler.+, Amperemeter.Positive
  N3: Raspberry/Galileo_Board.DC_in, Amperemeter.Com

custom parts:
  Mystery Part - 2 pins: A dummy, proxy, ersatz, stand-in part for whatever you want. With 2 pins on a 100 mil inline pin header footprint.
  Amperemeter: A Standard Multimeter in Current mode
